// Logisim project smips.circ as structural Verilog: 6 circuits, main circuit Board
module Board (
);

  wire CLK, HALT, MEM_WE, RESET, TTY_WE;
  wire [3:0] MEM_BE;
  wire [6:0] TTY_DATA;
  wire [31:0] MEM_ADDR, MEM_RDATA, MEM_WDATA;

  Clock Reloj (.out(CLK));
  Button u_Reset (.out(RESET));
  CPU cpu_1 (
    .CLK(CLK), .RESET(RESET), .MEM_RDATA(MEM_RDATA), .MEM_ADDR(MEM_ADDR), .MEM_WDATA(MEM_WDATA),
    .MEM_BE(MEM_BE), .MEM_WE(MEM_WE), .TTY_DATA(TTY_DATA), .TTY_WE(TTY_WE), .HALT(HALT));
  TTY #(.cols(48), .rows(12)) tty_1 (.data(TTY_DATA), .clk(CLK), .we(TTY_WE), .clr(RESET));
  Memory memory_1 (.CLK(CLK), .ADDR(MEM_ADDR), .WDATA(MEM_WDATA), .BE(MEM_BE), .WE(MEM_WE), .RDATA(MEM_RDATA));
  LED u_Halt (.in(HALT));

  // Notes on the sheet:
  //   S-MIPS | Board
  //   No modificar: la CPU se implementa dentro del subcircuito CPU.
endmodule

module CPU (
  input  CLK,
  input  RESET,
  input  [31:0] MEM_RDATA,
  output [31:0] MEM_ADDR,
  output [31:0] MEM_WDATA,
  output [3:0] MEM_BE,
  output MEM_WE,
  output [6:0] TTY_DATA,
  output TTY_WE,
  output HALT
);


  // Notes on the sheet:
  //   CPU S-MIPS: implementar aqui
  //   No cambiar nombres, anchos ni sentido de los pines: la placa depende de ellos.
endmodule

module Memory (
  input  CLK,
  input  [31:0] ADDR,
  input  [31:0] WDATA,
  input  [3:0] BE,
  input  WE,
  output [31:0] RDATA
);

  RAM #(.addrWidth(12), .asyncread("true"), .byteenables("byteEnables"), .dataWidth(32), .\type ("nonvolatile")) Main_Memory (
    .addr(ADDR[13:2]), .we(WE), .oe(1'b1), .clk(CLK), .din(WDATA), .dout(RDATA), .be3(BE[3]), .be2(BE[2]),
    .be1(BE[1]), .be0(BE[0]));

  // Other names for the same wires on the sheet: A[11:0] = ADDR[13:2]

  // Notes on the sheet:
  //   Memoria unificada: 4096 palabras de 32 bits (16 KiB), little-endian
  //   Lectura combinacional; escritura en el flanco de subida de CLK con WE=1, solo en los bytes con BE=1.
  //   Se usan los bits 13..2 de ADDR; los demas se ignoran (el espacio se repite cada 16 KiB).
endmodule

module ALU (
  input  [31:0] in_1,
  input  [31:0] in_2,
  input  [3:0] in_3,
  output [31:0] out_4,
  output out_5
);

  wire comparator_1_eq, comparator_1_gt, comparator_1_lt;
  wire [31:0] and_Gate, Div, Igual, Mayor, Menor, Mult, or_Gate, Resta, Resto, Suma, xor_Gate;

  Adder #(.width(32)) adder_1 (.a(in_1), .b(in_2), .out(Suma));  // open: cin, cout
  Subtractor #(.width(32)) subtractor_1 (.a(in_1), .b(in_2), .out(Resta));  // open: bin, bout
  Multiplier #(.mode("twosComplement"), .width(32)) multiplier_1 (.a(in_1), .b(in_2), .out(Mult));  // open: cin, cout
  Divider #(.mode("twosComplement"), .width(32)) divider_1 (.a(in_1), .b(in_2), .out(Div), .rem(Resto));  // open: upper
  Comparator #(.width(32)) comparator_1 (
    .a(in_1), .b(in_2), .gt(comparator_1_gt), .eq(comparator_1_eq), .lt(comparator_1_lt));
  assign and_Gate = in_1 & in_2;  // AND_Gate and_1, 32 bits wide
  assign or_Gate = in_1 | in_2;  // OR_Gate or_1, 32 bits wide
  assign xor_Gate = in_1 ^ in_2;  // XOR_Gate xor_1, 32 bits wide
  assign Mayor = {{31{comparator_1_gt}}, comparator_1_gt};  // Bit_Extender bit_extender_1
  assign Igual = {{31{comparator_1_eq}}, comparator_1_eq};  // Bit_Extender bit_extender_2
  assign Menor = {{31{comparator_1_lt}}, comparator_1_lt};  // Bit_Extender bit_extender_3
  Multiplexer #(.select(4), .width(32)) multiplexer_1 (
    .in0(Suma), .in1(Resta), .in2(Mult), .in3(Div), .in4(Resto), .in5(and_Gate), .in6(or_Gate),
    .in7(xor_Gate), .in8(Mayor), .in9(Igual), .in10(Menor), .out(out_4), .sel(in_3));  // open: in11, in12, in13, in14, in15
  Comparator #(.width(32)) comparator_2 (.a({32{1'b0}}), .b(out_4), .eq(out_5));  // open: gt, lt

  // Other names for the same wires on the sheet: Rd[31:0] = out_4; Rs[31:0] = in_1; Rt[31:0] = in_2;
  //   Selector_ALU[3:0] = in_3; zero = out_5

  // Notes on the sheet:
  //   Inputs
  //   Outputs
  //   ALU
endmodule

module RegisterFile (
  input  [31:0] in_1,
  input  [4:0] in_2,
  input  [4:0] in_3,
  input  [4:0] in_4,
  input  in_5,
  input  in_6,
  input  in_7,
  output [31:0] out_8,
  output [31:0] out_9
);

  wire En01, En02, En03, En04, En05, En06, En07, En08, En09, En10, En11, En12, En13, En14, En15, En16, En17,
       En18, En19, En20, En21, En22, En23, En24, En25, En26, En27, En28, En29, En30, En31;
  wire [31:0] RR00, RR01, RR02, RR03, RR04, RR05, RR06, RR07, RR08, RR09, RR10, RR11, RR12, RR13, RR14, RR15,
       RR16, RR17, RR18, RR19, RR20, RR21, RR22, RR23, RR24, RR25, RR26, RR27, RR28, RR29, RR30, RR31;

  Register #(.width(32)) register_1 (.clk(in_5), .Q(RR00));  // open: D, en, clr
  Register #(.width(32)) register_2 (.D(in_1), .en(En01), .clk(in_5), .Q(RR01), .clr(in_7));
  Register #(.width(32)) register_3 (.D(in_1), .en(En02), .clk(in_5), .Q(RR02), .clr(in_7));
  Register #(.width(32)) register_4 (.D(in_1), .en(En03), .clk(in_5), .Q(RR03), .clr(in_7));
  Register #(.width(32)) register_5 (.D(in_1), .en(En04), .clk(in_5), .Q(RR04), .clr(in_7));
  Register #(.width(32)) register_6 (.D(in_1), .en(En05), .clk(in_5), .Q(RR05), .clr(in_7));
  Register #(.width(32)) register_7 (.D(in_1), .en(En06), .clk(in_5), .Q(RR06), .clr(in_7));
  Register #(.width(32)) register_8 (.D(in_1), .en(En07), .clk(in_5), .Q(RR07), .clr(in_7));
  Register #(.width(32)) register_9 (.D(in_1), .en(En08), .clk(in_5), .Q(RR08), .clr(in_7));
  Register #(.width(32)) register_10 (.D(in_1), .en(En09), .clk(in_5), .Q(RR09), .clr(in_7));
  Register #(.width(32)) register_11 (.D(in_1), .en(En10), .clk(in_5), .Q(RR10), .clr(in_7));
  Register #(.width(32)) register_12 (.D(in_1), .en(En11), .clk(in_5), .Q(RR11), .clr(in_7));
  Demultiplexer #(.disabled("Z"), .select(5)) demultiplexer_1 (
    .out1(En01), .out2(En02), .out3(En03), .out4(En04), .out5(En05), .out6(En06), .out7(En07), .out8(En08),
    .out9(En09), .out10(En10), .out11(En11), .out12(En12), .out13(En13), .out14(En14), .out15(En15),
    .out16(En16), .out17(En17), .out18(En18), .out19(En19), .out20(En20), .out21(En21), .out22(En22),
    .out23(En23), .out24(En24), .out25(En25), .out26(En26), .out27(En27), .out28(En28), .out29(En29),
    .out30(En30), .out31(En31), .in(in_6), .sel(in_4));  // open: out0
  Register #(.width(32)) register_13 (.D(in_1), .en(En12), .clk(in_5), .Q(RR12), .clr(in_7));
  Register #(.width(32)) register_14 (.D(in_1), .en(En13), .clk(in_5), .Q(RR13), .clr(in_7));
  Register #(.width(32)) register_15 (.D(in_1), .en(En14), .clk(in_5), .Q(RR14), .clr(in_7));
  Register #(.width(32)) register_16 (.D(in_1), .en(En15), .clk(in_5), .Q(RR15), .clr(in_7));
  Register #(.width(32)) register_17 (.D(in_1), .en(En16), .clk(in_5), .Q(RR16), .clr(in_7));
  Register #(.width(32)) register_18 (.D(in_1), .en(En17), .clk(in_5), .Q(RR17), .clr(in_7));
  Multiplexer #(.select(5), .width(32)) multiplexer_1 (
    .in0(RR00), .in1(RR01), .in2(RR02), .in3(RR03), .in4(RR04), .in5(RR05), .in6(RR06), .in7(RR07),
    .in8(RR08), .in9(RR09), .in10(RR10), .in11(RR11), .in12(RR12), .in13(RR13), .in14(RR14), .in15(RR15),
    .in16(RR16), .in17(RR17), .in18(RR18), .in19(RR19), .in20(RR20), .in21(RR21), .in22(RR22), .in23(RR23),
    .in24(RR24), .in25(RR25), .in26(RR26), .in27(RR27), .in28(RR28), .in29(RR29), .in30(RR30), .in31(RR31),
    .out(out_8), .sel(in_2));
  Register #(.width(32)) register_19 (.D(in_1), .en(En18), .clk(in_5), .Q(RR18), .clr(in_7));
  Register #(.width(32)) register_20 (.D(in_1), .en(En19), .clk(in_5), .Q(RR19), .clr(in_7));
  Register #(.width(32)) register_21 (.D(in_1), .en(En20), .clk(in_5), .Q(RR20), .clr(in_7));
  Register #(.width(32)) register_22 (.D(in_1), .en(En21), .clk(in_5), .Q(RR21), .clr(in_7));
  Register #(.width(32)) register_23 (.D(in_1), .en(En22), .clk(in_5), .Q(RR22), .clr(in_7));
  Register #(.width(32)) register_24 (.D(in_1), .en(En23), .clk(in_5), .Q(RR23), .clr(in_7));
  Multiplexer #(.select(5), .width(32)) multiplexer_2 (
    .in0(RR00), .in1(RR01), .in2(RR02), .in3(RR03), .in4(RR04), .in5(RR05), .in6(RR06), .in7(RR07),
    .in8(RR08), .in9(RR09), .in10(RR10), .in11(RR11), .in12(RR12), .in13(RR13), .in14(RR14), .in15(RR15),
    .in16(RR16), .in17(RR17), .in18(RR18), .in19(RR19), .in20(RR20), .in21(RR21), .in22(RR22), .in23(RR23),
    .in24(RR24), .in25(RR25), .in26(RR26), .in27(RR27), .in28(RR28), .in29(RR29), .in30(RR30), .in31(RR31),
    .out(out_9), .sel(in_3));
  Register #(.width(32)) register_25 (.D(in_1), .en(En24), .clk(in_5), .Q(RR24), .clr(in_7));
  Register #(.width(32)) register_26 (.D(in_1), .en(En25), .clk(in_5), .Q(RR25), .clr(in_7));
  Register #(.width(32)) register_27 (.D(in_1), .en(En26), .clk(in_5), .Q(RR26), .clr(in_7));
  Register #(.width(32)) register_28 (.D(in_1), .en(En27), .clk(in_5), .Q(RR27), .clr(in_7));
  Register #(.width(32)) register_29 (.D(in_1), .en(En28), .clk(in_5), .Q(RR28), .clr(in_7));
  Register #(.width(32)) register_30 (.D(in_1), .en(En29), .clk(in_5), .Q(RR29), .clr(in_7));
  Register #(.width(32)) register_31 (.D(in_1), .en(En30), .clk(in_5), .Q(RR30), .clr(in_7));
  Register #(.width(32)) register_32 (.D(in_1), .en(En31), .clk(in_5), .Q(RR31), .clr(in_7));

  // Other names for the same wires on the sheet: A[31:0] = out_8; B[31:0] = out_9; clk = in_5; Data[31:0] = in_1;
  //   R_W = in_6; reset = in_7; SelectorA[4:0] = in_2; SelectorB[4:0] = in_3; SelectorData[4:0] = in_4

  // Notes on the sheet:
  //   Inputs
  //   Registers
  //   Selector Data
  //   Selector A
  //   Selector B
  //   Outputs
endmodule

module InstructionDecoder (
  input  [31:0] in_1,
  output [5:0] out_2,
  output [4:0] out_3,
  output [4:0] out_4,
  output [25:0] out_5,
  output [4:0] out_6,
  output [15:0] out_7,
  output [5:0] out_8
);


  assign out_2 = in_1[31:26];
  assign out_3 = in_1[25:21];
  assign out_4 = in_1[20:16];
  assign out_5 = in_1[25:0];
  assign out_6 = in_1[15:11];
  assign out_7 = in_1[15:0];
  assign out_8 = in_1[5:0];

  // Other names for the same wires on the sheet: const[15:0] = in_1[15:0]; func[5:0] = in_1[5:0];
  //   rute[25:0] = in_1[25:0]; Rd[4:0] = in_1[15:11]; Rt[4:0] = in_1[20:16]; Rs[4:0] = in_1[25:21];
  //   op[5:0] = in_1[31:26]

  // Notes on the sheet:
  //   Input
  //   Instruction Decoder
  //   Outputs
endmodule
